# Fritzing sketch compteurV1 (saved by Fritzing 0.9.3b)
breadboards: 1

parts:
  Composant1 = Arduino Uno (Rev3)
  hc-sr1 = hc-sr04
  U1 = LCD-16X2 [package=lcd-16x2_noholes]
  R1 = Rotary Potentiometer (Small) [maximum_resistance=10kΩ package=THT]
  R2 = Resistor [tolerance=±5% resistance=220 package=THT]

nets:
  N1: Composant1.D8, hc-sr1.Echo
  N2: Composant1.D9_PWM, hc-sr1.Trig
  N3: Composant1.D11_PWM/MOSI, U1.E
  N4: Composant1.D12/MISO, U1.VO, U1.RS, R1.wiper
  N5: Composant1.D2, U1.DB7
  N6: Composant1.D3_PWM, U1.DB6
  N7: Composant1.D4, U1.DB5
  N8: Composant1.D5_PWM, U1.DB4
  5V: Composant1.5V, hc-sr1.VCC, U1.VDD, R1.leg2, R2.Pin_1
  GND: Composant1.GND, hc-sr1.GND, U1.VSS, U1.R_W, U1.K, R1.leg1
  N9: U1.A, R2.Pin_0
