# Fritzing sketch COMPTEUR_simple (saved by Fritzing 0.9.3b)
breadboards: 1

parts:
  Arduino_Uno = Arduino Uno (Rev3)
  Afficheur_LCD = LCD-16X2 [package=lcd-16x2_noholes]
  Potentiomètre_10kΩ = Rotary Potentiometer (Small) [maximum_resistance=10kΩ package=THT]
  Résistance_220Ω = Resistor [tolerance=±5% resistance=220 package=THT]
  Module_Ultrason_HC-SR5 = hc-sr04
  Shield_SD/RTC = Memoire 1.0 - SD card log shield

nets:
  N1: Arduino_Uno.A0, Module_Ultrason_HC-SR5.Trig
  N2: Arduino_Uno.A1, Module_Ultrason_HC-SR5.Echo
  5V: Arduino_Uno.5V, Afficheur_LCD.VDD, Potentiomètre_10kΩ.leg2, Résistance_220Ω.Pin_0, Module_Ultrason_HC-SR5.VCC
  GND: Arduino_Uno.GND, Afficheur_LCD.VSS, Afficheur_LCD.R_W, Afficheur_LCD.K, Potentiomètre_10kΩ.leg1, Module_Ultrason_HC-SR5.GND
  N3: Afficheur_LCD.VO, Potentiomètre_10kΩ.wiper
  N4: Afficheur_LCD.RS, Shield_SD/RTC.DIG_9
  N5: Afficheur_LCD.E, Shield_SD/RTC.DIG_8
  N6: Afficheur_LCD.DB4, Shield_SD/RTC.DIG_5
  N7: Afficheur_LCD.DB5, Shield_SD/RTC.DIG_3
  N8: Afficheur_LCD.DB6, Shield_SD/RTC.DIG_2
  N9: Afficheur_LCD.DB7, Shield_SD/RTC.DIG_0
  N10: Afficheur_LCD.A, Résistance_220Ω.Pin_1
